# Fritzing sketch MEARM (saved by Fritzing 0.9.3b)
breadboards: 1

parts:
  Part1 = Arduino Uno (Rev3)
  R2 = Rotary Potentiometer (Small) [maximum_resistance=100kΩ package=THT]
  R3 = Rotary Potentiometer (Small) [maximum_resistance=100kΩ package=THT]
  R4 = Rotary Potentiometer (Small) [maximum_resistance=100kΩ package=THT]
  R5 = Rotary Potentiometer (Small) [maximum_resistance=100kΩ package=THT]
  M4 = Dagu DGServo 9g (End View) [part_number=RS001B]
  M5 = Dagu DGServo 9g (End View) [part_number=RS001B]
  M6 = Dagu DGServo 9g (End View) [part_number=RS001B]
  M7 = Dagu DGServo 9g (End View) [part_number=RS001B]

nets:
  N1: Part1.A0, R2.wiper
  N2: Part1.A1, R3.wiper
  N3: Part1.A2, R4.wiper
  N4: Part1.A3, R5.wiper
  N5: Part1.D9_PWM, M5.pulse
  N6: Part1.D10_PWM/SS, M6.pulse
  N7: Part1.D11_PWM/MOSI, M7.pulse
  N8: Part1.D5_PWM, M4.pulse
  VCC: Part1.5V, R2.leg2, R3.leg2, R4.leg2, R5.leg2, M4.vcc, M5.vcc, M6.vcc, M7.vcc
  GND: Part1.GND, R2.leg1, R3.leg1, R4.leg1, R5.leg1, M4.gnd, M5.gnd, M6.gnd, M7.gnd

// code stored in the sketch: mearm.ino

int potentiometerPin = 0;


int ledPin = 11;

int potentiometerVal = 0;



void setup()

{

  Serial.begin(9600);          //  setup serial

}



void loop()

{

  potentiometerVal = analogRead(potentiometerPin);

 

 //I use the map function because PWM pins can only accept

 //values from 0 to 255. Analog pins can output values from

 //0 to 1023. With the map function, the range 0-1023 is 

 //converted to appropriate values from 0 to 255.

 int mappedVal = map(potentiometerVal,0,1023,0,255);

 Serial.print(potentiometerVal);

 Serial.print(" - ");

 Serial.println(mappedVal);

 analogWrite(ledPin,mappedVal);

 delay(10); 

}
